# Fritzing sketch 02_3LED_Blink (saved by Fritzing 0.9.4)
breadboards: 1

parts:
  R3 = Resistor [tolerance=±5% resistance=330 package=THT]  # not connected
  LED3 = LED - 5mm [color="Green (570nm)" package="5 mm [THT]"]
  LED1 = LED - 5mm [color="Red (633nm)" package="5 mm [THT]"]
  R2 = Resistor [tolerance=±5% resistance=330 package=THT]
  LED2 = LED - 5mm [color="Blue (525nm)" package="5 mm [THT]"]
  Part1 = Arduino Uno (Rev3)
  R1 = Resistor [tolerance=±5% resistance=330 package=THT]  # not connected

nets:
  N1: LED3.cathode, LED1.cathode, LED2.cathode, Part1.GND
  N2: R2.Pin_0, Part1.D7
  N3: R2.Pin_1, LED2.anode

// code stored in the sketch: 02_3LED_Blink.ino

/*
  Blinking LEDs

  Turns each LED of 3 for one second, then off for one second, repeatedly.

   The circuit:
  - RED LED attached from digital pin 5 to ground.
  - GREEN LED attached from digital pin 6 to ground.
  - BLUE LED attached from digital pin 7 to ground.

  by Ganesh Butcha
*/


int led1=5;               // assign digital pin 5 to a variable
int led2=6;
int led3=7;
int waitTime=1000;        // wait time is 1 second

void setup() {
  // put your setup code here, to run once:
  pinMode(led1, OUTPUT);    // initialize digital pin as an output
  pinMode(led2, OUTPUT);    
  pinMode(led3, OUTPUT);

}

void loop() {
  // put your main code here, to run repeatedly:
  digitalWrite(led1, HIGH);   // turn the LED on (HIGH is the voltage level)
  digitalWrite(led2, LOW);    // turn the LED off (LOW is the voltage level)
  digitalWrite(led3, LOW);
  delay(waitTime);                 // wait for a second
  
  digitalWrite(led1, LOW);
  digitalWrite(led2, HIGH);
  digitalWrite(led3, LOW);
  delay(waitTime);

  digitalWrite(led1, LOW);
  digitalWrite(led2, LOW);
  digitalWrite(led3, HIGH);
  delay(waitTime);
  
}
