# Fritzing sketch 05_PhotoResistors (saved by Fritzing 0.9.4)
circuit board: 8.46667cm x 5.64444cm
breadboards: 1

parts:
  Part1 = Arduino Uno (Rev3)
  LED1 = LED - 5mm [color="Green (570nm)" package="5 mm [THT]"]
  R1 = Resistor [tolerance=±5% resistance=330 package=THT]
  LED2 = LED - 5mm [color="Red (633nm)" package="5 mm [THT]"]
  R2 = Resistor [tolerance=±5% resistance=330 package=THT]
  R3 = Photocell (LDR) [package=THT]
  R4 = Resistor [tolerance=±5% resistance=4.7k package=THT]

nets:
  N1: Part1.A0, R3.pin_0, R4.Pin_1
  N2: Part1.GND, LED1.cathode, LED2.cathode, R4.Pin_0
  N3: Part1.D2, R1.Pin_1
  N4: Part1.D4, R2.Pin_1
  N5: Part1.5V, R3.pin_1
